// Logisim project 7483_corrected.circ as structural Verilog: 2 circuits, main circuit main
// S1
module main (
  input  A4,
  input  A3,
  input  A2,
  input  A1,
  input  B4,
  input  B3,
  input  B2,
  input  B1,
  input  Cin,
  output S4,
  output S3,
  output S2,
  output S1,
  output Cout
);

  _7483_new u_7483_new_1 (
    ._1__A4(A4), ._2__S3(S3), ._3__A3(A3), ._4__B3(B3), ._6__S2(S2), ._7__B2(B2), ._8__A2(A2), ._16__B4(B4),
    ._15__S4(S4), ._14__Cout(Cout), ._13__Cin(Cin), ._11__B1(B1), ._10__A1(A1), ._9__S1(S1));  // open: _5__Vcc, _12__GND
endmodule

module _7483_new (
  input  _1__A4,
  input  _16__B4,
  input  _3__A3,
  input  _4__B3,
  input  _13__Cin,
  input  _5__Vcc,
  input  _12__GND,
  input  _11__B1,
  input  _7__B2,
  input  _10__A1,
  input  _8__A2,
  output _2__S3,
  output _15__S4,
  output _14__Cout,
  output _6__S2,
  output _9__S1
);

  wire and_1_out, and_2_out, and_3_out, and_4_out, and_5_out, and_6_out, and_7_out, and_8_out, and_9_out,
       and_10_out, and_11_out, and_12_out, and_13_out, and_14_out, nand_1_out, nand_2_out, nand_3_out,
       nand_4_out, nor_1_out, nor_2_out, nor_3_out, nor_4_out, nor_6_out, nor_7_out, nor_8_out, not_1_out,
       not_2_out, not_3_out, not_4_out, not_5_out, not_6_out;

  nand nand_1 (nand_1_out, _16__B4, _1__A4);
  nor nor_1 (nor_1_out, _16__B4, _1__A4);
  nand nand_2 (nand_2_out, _4__B3, _3__A3);
  nor nor_2 (nor_2_out, _4__B3, _3__A3);
  nand nand_3 (nand_3_out, _7__B2, _8__A2);
  nor nor_3 (nor_3_out, _7__B2, _8__A2);
  nand nand_4 (nand_4_out, _11__B1, _10__A1);
  nor nor_4 (nor_4_out, _11__B1, _10__A1);
  and and_1 (and_1_out, nor_2_out, nand_1_out);
  and and_2 (and_2_out, nor_3_out, nand_1_out, nand_2_out);
  and and_3 (and_3_out, nor_4_out, nand_1_out, nand_2_out, nand_3_out);
  and and_4 (and_4_out, nand_1_out, nand_2_out, nand_3_out, nand_4_out, not_2_out);
  not not_1 (not_1_out, nor_1_out);
  and and_5 (and_5_out, nor_3_out, nand_2_out);
  and and_6 (and_6_out, nor_4_out, nand_2_out, nand_3_out);
  and and_7 (and_7_out, nand_2_out, nand_3_out, nand_4_out, not_2_out);
  not not_2 (not_2_out, _13__Cin);
  not not_3 (not_3_out, nor_2_out);
  and and_8 (and_8_out, nor_4_out, nand_3_out);
  and and_9 (and_9_out, nand_3_out, nand_4_out, not_2_out);
  not not_4 (not_4_out, nor_3_out);
  and and_10 (and_10_out, nand_4_out, not_2_out);
  not not_5 (not_5_out, nor_4_out);
  not not_6 (not_6_out, not_2_out);
  nor nor_5 (_14__Cout, nor_1_out, and_1_out, and_2_out, and_3_out, and_4_out);
  and and_11 (and_11_out, nand_1_out, not_1_out);
  and and_12 (and_12_out, nand_2_out, not_3_out);
  and and_13 (and_13_out, nand_3_out, not_4_out);
  and and_14 (and_14_out, nand_4_out, not_5_out);
  xor xor_1 (_15__S4, and_11_out, nor_6_out);
  nor nor_6 (nor_6_out, nor_2_out, and_5_out, and_6_out, and_7_out);
  xor xor_2 (_2__S3, and_12_out, nor_7_out);
  nor nor_7 (nor_7_out, nor_3_out, and_8_out, and_9_out);
  xor xor_3 (_6__S2, and_13_out, nor_8_out);
  nor nor_8 (nor_8_out, nor_4_out, and_10_out);
  xor xor_4 (_9__S1, and_14_out, not_6_out);

  // Notes on the sheet:
  //   7483: 4-bit full adder
endmodule
