// Logisim project block_diagram_new.circ as structural Verilog: 1 circuit, main circuit main
module main (
  input  cs0,
  input  cs1,
  input  cs2,
  input  in_4,
  input  A0,
  input  A1,
  input  A2,
  input  A3,
  input  in_9,
  input  B0,
  input  in_11,
  input  B1,
  input  B2,
  input  in_14,
  input  B3,
  output F0,
  output F1,
  output F2,
  output F3,
  output Z,
  output S,
  output V,
  output C
);

  wire and_1_out, and_2_out, and_3_out, and_4_out, and_5_out, main_1_cout, main_1_s1, main_2_cout, main_2_s1,
       main_2_s2, multiplexer_1_out, multiplexer_2_out, multiplexer_3_out, multiplexer_4_out, not_1_out,
       not_2_out, not_3_out, not_4_out, not_5_out, not_6_out, or_1_out, or_2_out, or_3_out, xor_1_out,
       xor_2_out, xor_3_out, xor_4_out, xor_5_out, xor_6_out;

  xor xor_1 (xor_1_out, cs1, cs0);
  not not_1 (not_1_out, cs2);
  and and_1 (and_1_out, cs0, not_1_out);
  and and_2 (and_2_out, and_1_out, cs1);
  xor xor_2 (xor_2_out, xor_1_out, B0);
  xor xor_3 (xor_3_out, xor_1_out, B1);
  xor xor_4 (xor_4_out, xor_1_out, B2);
  xor xor_5 (xor_5_out, xor_1_out, B3);
  not not_2 (not_2_out, cs1);
  not not_3 (not_3_out, cs0);
  Multiplexer multiplexer_1 (.in0(xor_2_out), .in1(and_2_out), .out(multiplexer_1_out), .sel(cs2));  // open: en
  Multiplexer multiplexer_2 (.in0(xor_3_out), .in1(and_2_out), .out(multiplexer_2_out), .sel(cs2));  // open: en
  Multiplexer multiplexer_3 (.in0(xor_4_out), .in1(and_2_out), .out(multiplexer_3_out), .sel(cs2));  // open: en
  Multiplexer multiplexer_4 (.in0(xor_5_out), .in1(and_2_out), .out(multiplexer_4_out), .sel(cs2));  // open: en
  and and_3 (and_3_out, and_1_out, not_2_out);
  and and_4 (and_4_out, not_3_out, cs1);
  not not_4 (not_4_out, and_2_out);
  or or_1 (or_1_out, and_3_out, and_4_out);
  parallel_adder_main main_1 (
    .A3(A1), .A2(not_4_out), .B2(main_1_s1), .S1(main_1_s1), .B1(in_9), .A1(in_4), .S0(F0), .A0(A0),
    .B0(multiplexer_1_out), .B3(multiplexer_2_out), .Cin(or_1_out), .S3(F1), .Cout(main_1_cout));  // open: S2
  parallel_adder_main main_2 (
    .A3(A3), .A2(not_4_out), .B2(main_2_s1), .S1(main_2_s1), .S2(main_2_s2), .B1(in_14), .A1(in_11), .S0(F2),
    .A0(A2), .B0(multiplexer_3_out), .B3(multiplexer_4_out), .Cin(and_5_out), .S3(F3), .Cout(main_2_cout));
  and and_5 (and_5_out, not_4_out, main_1_cout);
  or or_2 (or_2_out, F1, F0);
  or or_3 (or_3_out, F2, F3);
  xor xor_6 (xor_6_out, main_2_s1, main_2_cout);
  not not_5 (not_5_out, or_2_out);
  not not_6 (not_6_out, or_3_out);
  and and_6 (Z, not_5_out, not_6_out);
  and and_7 (V, xor_6_out, not_4_out);
  and and_8 (C, main_2_cout, not_4_out);

  assign S = F3;
endmodule
