// Logisim project block_diagram_old.circ as structural Verilog: 1 circuit, main circuit main
module main (
  input  Ai,
  input  CS0,
  input  Bi_XOR_CS__XOR_CS0,
  input  S1,
  output F3,
  output F2,
  output F1,
  output F0,
  output C,
  output V,
  output Z,
  output S
);

  wire multiplexer_1_out, n7483_1__2__s3, n7483_1__6__s2, n7483_1__9__s1, n7483_2__2__s3, n7483_2__9__s1,
       n7483_2__14__cout, not_1_out, not_2_out, or_1_out, or_2_out, undriven, undriven_2, undriven_3,
       undriven_4, undriven_5, undriven_6, undriven_7, undriven_8, xor_1_out;

  Multiplexer multiplexer_1 (.in0(CS0), .in1(Bi_XOR_CS__XOR_CS0), .out(multiplexer_1_out), .en(S1));  // open: sel
  _7483 u_7483_1 (
    ._1__A4(Ai), ._2__S3(n7483_1__2__s3), ._3__A3(undriven_3), ._4__B3(Ai), ._5__Vcc(multiplexer_1_out),
    ._6__S2(n7483_1__6__s2), ._7__B2(undriven_3), ._8__A2(multiplexer_1_out), ._16__B4(undriven_8),
    ._15__S4(F3), ._13__Cin(undriven_4), ._12__GND(F2), ._9__S1(n7483_1__9__s1));  // open: _14__Cout, _11__B1, _10__A1
  and and_1 (n7483_1__9__s1, undriven_5, undriven_6);
  _7483 u_7483_2 (
    ._1__A4(Ai), ._2__S3(n7483_2__2__s3), ._3__A3(undriven), ._4__B3(Ai), ._5__Vcc(multiplexer_1_out),
    ._6__S2(n7483_2__2__s3), ._7__B2(undriven_2), ._8__A2(multiplexer_1_out), ._16__B4(undriven_6),
    ._15__S4(F1), ._14__Cout(n7483_2__14__cout), ._12__GND(F0), ._9__S1(n7483_2__9__s1));  // open: _13__Cin, _11__B1, _10__A1
  xor xor_1 (xor_1_out, undriven_8, undriven_4);
  and and_2 (C, undriven_7, undriven_8);
  and and_3 (V, xor_1_out, undriven_7);
  or or_1 (or_1_out, F0, F1);
  or or_2 (or_2_out, F2, F3);
  not not_1 (not_1_out, or_1_out);
  not not_2 (not_2_out, or_2_out);
  and and_4 (Z, not_1_out, not_2_out);

  assign S = F3;

  // Notes on the sheet:
  //   B1
  //   A3
  //   A2
  //   B3
  //   A1
  //   A0
  //   B0
  //   C3
  //   S2'
  //   B2
  //   S2'
  //   C1
  //   0
  //   0
  //   C2
  //   S2'
  //   S2'
  //   Zin
  //   C4
  //   C3
  //   C1
endmodule
