// Logisim project offline1_alu_c1_gr_3.circ as structural Verilog: 1 circuit, main circuit main
module main (
  input  A3,
  input  A2,
  input  A1,
  input  A0,
  input  B3,
  input  B2,
  input  B1,
  input  B0,
  input  CS2,
  input  CS1,
  input  CS0,
  output Cout,
  output F3,
  output F2,
  output F1,
  output F0,
  output C,
  output S,
  output V,
  output Z
);

  wire n7404_1__2__1y, n7404_1__4__2y, n7404_1__6__3y, n7404_1__8__4y, n7404_1__10__5y, n7404_1__12__6y,
       n7408_1__3__1y, n7408_1__6__2y, n7408_1__11__4y, n7408_2__3__1y, n7408_2__11__4y, n7432_1__3__1y,
       n7432_1__8__3y, n7432_1__11__4y, n7483_1__6__s2, n7483_2__6__s2, n7483_2__14__cout, n7486_1__3__1y,
       n7486_1__11__4y, n7486_2__3__1y, n7486_2__6__2y, n7486_2__8__3y, n7486_2__11__4y, n74157_1__4__y1,
       n74157_1__7__y2, n74157_1__9__y3, n74157_1__12__y4;

  _7404 u_7404_1 (
    ._1__1A(CS2), ._2__1Y(n7404_1__2__1y), ._3__2A(CS1), ._4__2Y(n7404_1__4__2y), ._5__3A(CS0),
    ._6__3Y(n7404_1__6__3y), ._13__6A(n7408_1__6__2y), ._12__6Y(n7404_1__12__6y), ._11__5A(n7432_1__11__4y),
    ._10__5Y(n7404_1__10__5y), ._9__4A(n7432_1__8__3y), ._8__4Y(n7404_1__8__4y));  // open: _7__GND, _14__Vcc
  _7486 u_7486_1 (
    ._1__1A(CS1), ._2__1B(CS0), ._3__1Y(n7486_1__3__1y), ._13__4B(Cout), ._12__4A(n7483_1__6__s2),
    ._11__4Y(n7486_1__11__4y));  // open: _4__2A, _5__2B, _6__2Y, _7__GND, _14__Vcc, _10__3B, _9__3A, _8__3Y
  _7408 u_7408_1 (
    ._1__1A(n7404_1__2__1y), ._2__1B(CS0), ._3__1Y(n7408_1__3__1y), ._4__2A(n7408_1__3__1y), ._5__2B(CS1),
    ._6__2Y(n7408_1__6__2y), ._13__4B(n7408_1__3__1y), ._12__4A(n7404_1__4__2y), ._11__4Y(n7408_1__11__4y),
    ._10__3B(n7404_1__10__5y), ._9__3A(n7404_1__8__4y), ._8__3Y(Z));  // open: _7__GND, _14__Vcc
  _7432 u_7432_1 (
    ._1__1A(n7408_2__3__1y), ._2__1B(n7408_1__11__4y), ._3__1Y(n7432_1__3__1y), ._13__4B(F3), ._12__4A(F2),
    ._11__4Y(n7432_1__11__4y), ._10__3B(F1), ._9__3A(F0), ._8__3Y(n7432_1__8__3y));  // open: _4__2A, _5__2B, _6__2Y, _7__GND, _14__Vcc
  _7408 u_7408_2 (
    ._1__1A(CS2), ._2__1B(n7404_1__6__3y), ._3__1Y(n7408_2__3__1y), ._4__2A(Cout), ._5__2B(n7404_1__12__6y),
    ._6__2Y(C), ._13__4B(n7483_2__14__cout), ._12__4A(n7404_1__12__6y), ._11__4Y(n7408_2__11__4y),
    ._10__3B(n7486_1__11__4y), ._9__3A(n7404_1__12__6y), ._8__3Y(V));  // open: _7__GND, _14__Vcc
  _7483 u_7483_1 (
    ._1__A4(A3), ._3__A3(n7404_1__12__6y), ._4__B3(n7483_1__6__s2), ._6__S2(n7483_1__6__s2), ._7__B2(1'b0),
    ._8__A2(1'b0), ._16__B4(n74157_1__4__y1), ._15__S4(F3), ._14__Cout(Cout), ._13__Cin(n7408_2__11__4y),
    ._11__B1(n74157_1__7__y2), ._10__A1(A2), ._9__S1(F2));  // open: _2__S3, _5__Vcc, _12__GND
  _7486 u_7486_2 (
    ._1__1A(B3), ._2__1B(n7486_1__3__1y), ._3__1Y(n7486_2__3__1y), ._4__2A(B2), ._5__2B(n7486_1__3__1y),
    ._6__2Y(n7486_2__6__2y), ._13__4B(B0), ._12__4A(n7486_1__3__1y), ._11__4Y(n7486_2__11__4y), ._10__3B(B1),
    ._9__3A(n7486_1__3__1y), ._8__3Y(n7486_2__8__3y));  // open: _7__GND, _14__Vcc
  _74157 u_74157_1 (
    ._1__S(n7404_1__2__1y), ._2__A1(CS0), ._3__B1(n7486_2__3__1y), ._4__Y1(n74157_1__4__y1), ._5__A2(CS0),
    ._6__B2(n7486_2__6__2y), ._7__Y2(n74157_1__7__y2), ._15__G(1'b0), ._14__A4(CS0),
    ._13__B4(n7486_2__11__4y), ._12__Y4(n74157_1__12__y4), ._11__A3(CS0), ._10__B3(n7486_2__8__3y),
    ._9__Y3(n74157_1__9__y3));  // open: _8__GND, _16__Vcc
  _7483 u_7483_2 (
    ._1__A4(A1), ._3__A3(n7404_1__12__6y), ._4__B3(n7483_2__6__s2), ._6__S2(n7483_2__6__s2), ._7__B2(1'b0),
    ._8__A2(1'b0), ._16__B4(n74157_1__9__y3), ._15__S4(F1), ._14__Cout(n7483_2__14__cout),
    ._13__Cin(n7432_1__3__1y), ._11__B1(n74157_1__12__y4), ._10__A1(A0), ._9__S1(F0));  // open: _2__S3, _5__Vcc, _12__GND

  assign S = F3;
endmodule
