// Logisim project parallel_adder.circ as structural Verilog: 1 circuit, main circuit main
module main (
  input  A0,
  input  A1,
  input  A2,
  input  A3,
  input  Cin,
  input  B0,
  input  B1,
  input  B2,
  input  B3,
  output Cout,
  output S0,
  output S1,
  output S2,
  output S3
);

  _7483_new u_7483_new_1 (
    ._1__A4(A3), ._2__S3(S2), ._3__A3(A2), ._4__B3(B2), ._5__Vcc(1'b1), ._6__S2(S1), ._7__B2(B1),
    ._8__A2(A1), ._16__B4(B3), ._15__S4(S3), ._14__Cout(Cout), ._13__Cin(Cin), ._12__GND(1'b0), ._11__B1(B0),
    ._10__A1(A0), ._9__S1(S0));
endmodule
