// Logisim project input_splitter.circ as structural Verilog: 2 circuits, main circuit main
module main (
  input  [31:0] in_1,
  output [21:0] out_2,
  output [8:0] out_3,
  output out_4
);


  assign out_2 = in_1[31:10];
  assign out_3 = in_1[9:1];
  assign out_4 = in_1[0];
endmodule

module demo (
);

  main main_1 ();  // open: in_1, out_4, out_3, out_2
endmodule
