// Logisim project FPA_IO.circ as structural Verilog: 11 circuits, main circuit main
module main (
  input  [31:0] in_1,
  input  [31:0] in_2,
  output [31:0] out_3,
  output out_4,
  output out_5,
  output ZERO,
  output NAN,
  output INF,
  output DeNorm
);

  wire BIG_EXP, FULL_SFT, not_1_out, O_P_SIGN, SIGN_A, SIGN_B, TEMP_OF;
  wire [4:0] SHIFT;
  wire [8:0] DENORM_EXP, EXP_A, EXP_B, O_P_EXP, TEMP_O_P_EXP;
  wire [21:0] FRAC_1, FRAC_2, FRAC_A, FRAC_B, O_P_FRACTION;
  wire [29:0] NON_ROUNDED_SUM;
  wire [31:0] DENORM_SUM, F_FRAC_A, significant_formatter_2_out_2, SNF_FRAC_B;

  input_handler input_handler_1 (.in_1(in_1), .FRAC(FRAC_A), .EXP(EXP_A), .SIGN(SIGN_A));
  exponent_differentiator exponent_differentiator_1 (
    .Ea(EXP_A), .Eb(EXP_B), .out_3(BIG_EXP), .SFT(SHIFT), .FULL_SFT(FULL_SFT));
  Multiplexer #(.width(9), .enable("false")) multiplexer_1 (.in0(EXP_A), .in1(EXP_B), .out(DENORM_EXP), .sel(BIG_EXP));
  output_handler output_handler_1 (
    .O_P(out_3), .FRAC(O_P_FRACTION), .EXP(O_P_EXP), .SIGN(O_P_SIGN), .NAN(NAN), .INF(INF), .DeNorm(DeNorm));
  input_handler input_handler_2 (.in_1(in_2), .FRAC(FRAC_B), .EXP(EXP_B), .SIGN(SIGN_B));
  normalizer normalizer_1 (
    .in_1(DENORM_SUM), .in_2(DENORM_EXP), .out_4(TEMP_O_P_EXP), .Overflow(TEMP_OF), .out_3(NON_ROUNDED_SUM),
    .Underflow(out_4));
  _32bit_alu u_32bit_alu_1 (
    .in_1(SIGN_A), .in_2(SIGN_B), .in_3(F_FRAC_A), .in_4(SNF_FRAC_B), .OUTPUT_SUM(DENORM_SUM),
    .O_P_S(O_P_SIGN), .in_5(BIG_EXP));
  Multiplexer #(.width(22), .enable("false")) multiplexer_2 (.in0(FRAC_A), .in1(FRAC_B), .out(FRAC_1), .sel(BIG_EXP));
  significant_formatter significant_formatter_1 (.in_1(FRAC_1), .out_2(F_FRAC_A));
  significant_formatter significant_formatter_2 (.in_1(FRAC_2), .out_2(significant_formatter_2_out_2));
  zero_flag zero_flag_1 (.in_1(in_1), .in_2(in_2), .ZERO_FLAG(ZERO));
  Multiplexer #(.width(22), .enable("false")) multiplexer_3 (.in0(FRAC_A), .in1(FRAC_B), .out(FRAC_2), .sel(not_1_out));
  not not_1 (not_1_out, BIG_EXP);
  shifter shifter_1 (
    .significant(significant_formatter_2_out_2), .SFT(SHIFT), .L_R_SFT(1'b1), .FULL_SFT(FULL_SFT),
    .out_5(SNF_FRAC_B));
  rounder rounder_1 (
    .in_1(NON_ROUNDED_SUM), .in_2(TEMP_O_P_EXP), .in_3(TEMP_OF), .O_P_FRACTION(O_P_FRACTION),
    .O_P_EXP(O_P_EXP), .OVERFLOW(out_5));

  // Other names for the same wires on the sheet: A[31:0] = in_1; B[31:0] = in_2; OVERFLOW = out_5; UNDERFLOW = out_4
endmodule

module exponent_differentiator (
  input  [8:0] Ea,
  input  [8:0] Eb,
  output out_3,
  output [4:0] SFT,
  output FULL_SFT
);

  wire not_1_out;
  wire [8:0] EXP_DEF, negator_1_out;
  wire [8:5] ABS_EXP_DEF;

  Subtractor #(.width(9)) subtractor_1 (.a(Ea), .b(Eb), .out(EXP_DEF), .bout(out_3));  // open: bin
  Negator #(.width(9)) negator_1 (.in(EXP_DEF), .out(negator_1_out));
  or or_1 (FULL_SFT, ABS_EXP_DEF[5], ABS_EXP_DEF[6], ABS_EXP_DEF[7], ABS_EXP_DEF[8]);
  Multiplexer #(.width(9), .enable("false")) multiplexer_1 (
    .in0(negator_1_out), .in1(EXP_DEF), .out({ABS_EXP_DEF, SFT}), .sel(not_1_out));
  not not_1 (not_1_out, out_3);

  // Other names for the same wires on the sheet: ABS_EXP_DEF[4:0] = SFT; BIG_EXP = out_3
endmodule

module shifter (
  input  [31:0] significant,
  input  [4:0] SFT,
  input  L_R_SFT,
  input  FULL_SFT,
  output [31:0] out_5
);

  wire [31:0] LFT_SFT, RHT_SFT;

  Shifter #(.width(32), .shift("lr")) shifter_1 (.in(significant), .\dist (SFT), .out(RHT_SFT));
  Shifter #(.width(32)) shifter_2 (.in(significant), .\dist (SFT), .out(LFT_SFT));
  Multiplexer #(.select(2), .width(32), .enable("false")) multiplexer_1 (
    .in0(LFT_SFT), .in1(RHT_SFT), .in2({32{1'b0}}), .in3({32{1'b0}}), .out(out_5), .sel({FULL_SFT, L_R_SFT}));
endmodule

module significant_formatter (
  input  [21:0] in_1,
  output [31:0] out_2
);


  assign out_2 = {2'b01, in_1, {8{1'b0}}};
endmodule

module normalizer (
  input  [31:0] in_1,
  input  [8:0] in_2,
  output [29:0] out_3,
  output [8:0] out_4,
  output Overflow,
  output Underflow
);

  wire adder_1_cout, all_1_1_out_2, not_2_out, priority_encoder_1_gs, R_L_SHFT, subtractor_1_bout;
  wire [4:0] not_1_out, priority_encoder_1_out, R_SHFT_AMNT, SHFT_AMNT;
  wire [8:0] adder_1_out, subtractor_1_out;
  wire [31:30] shifter_1_out_5;

  // Probe on in_1[31:30]
  assign not_1_out = ~priority_encoder_1_out;  // NOT_Gate not_1, 5 bits wide
  Priority_Encoder #(.select(5)) priority_encoder_1 (
    .in0(1'b0), .in1(in_1[0]), .in2(in_1[1]), .in3(in_1[2]), .in4(in_1[3]), .in5(in_1[4]), .in6(in_1[5]),
    .in7(in_1[6]), .in8(in_1[7]), .in9(in_1[8]), .in10(in_1[9]), .in11(in_1[10]), .in12(in_1[11]),
    .in13(in_1[12]), .in14(in_1[13]), .in15(in_1[14]), .in16(in_1[15]), .in17(in_1[16]), .in18(in_1[17]),
    .in19(in_1[18]), .in20(in_1[19]), .in21(in_1[20]), .in22(in_1[21]), .in23(in_1[22]), .in24(in_1[23]),
    .in25(in_1[24]), .in26(in_1[25]), .in27(in_1[26]), .in28(in_1[27]), .in29(in_1[28]), .in30(in_1[29]),
    .in31(1'b0), .out(priority_encoder_1_out), .gs(priority_encoder_1_gs));  // open: en_out, en_in
  Multiplexer #(.width(5), .enable("false")) multiplexer_1 (
    .in0({5{1'b0}}), .in1(not_1_out), .out(R_SHFT_AMNT), .sel(priority_encoder_1_gs));
  // Probe on R_SHFT_AMNT
  or or_1 (R_L_SHFT, in_1[30], in_1[31]);
  Multiplexer #(.width(5), .enable("false")) multiplexer_2 (
    .in0(R_SHFT_AMNT), .in1({4'b0000, in_1[31]}), .out(SHFT_AMNT), .sel(R_L_SHFT));
  Subtractor #(.width(9)) subtractor_1 (
    .a(in_2), .b({4'b0000, SHFT_AMNT}), .out(subtractor_1_out), .bout(subtractor_1_bout));  // open: bin
  Adder #(.width(9)) adder_1 (.a(in_2), .b({4'b0000, SHFT_AMNT}), .out(adder_1_out), .cout(adder_1_cout));  // open: cin
  not not_2 (not_2_out, in_1[31]);
  and and_1 (Underflow, subtractor_1_bout, not_2_out);
  Multiplexer #(.width(9), .enable("false")) multiplexer_3 (
    .in0(subtractor_1_out), .in1(adder_1_out), .out(out_4), .sel(in_1[31]));
  all_1 all_1_1 (.in_1(in_2), .out_2(all_1_1_out_2));
  or or_2 (Overflow, adder_1_cout, all_1_1_out_2);
  shifter shifter_1 (
    .significant(in_1), .SFT(SHFT_AMNT), .L_R_SFT(R_L_SHFT), .FULL_SFT(1'b0), .out_5({shifter_1_out_5, out_3}));

  // Other names for the same wires on the sheet: _31th_bit = in_1[31]; Output_Sum[31:0] = in_1;
  //   Output_EXP[8:0] = in_2; Fraction[29:0] = in_1[29:0]
endmodule

module _32bit_alu (
  input  in_1,
  input  in_2,
  input  [31:0] in_3,
  input  [31:0] in_4,
  input  in_5,
  output [31:0] OUTPUT_SUM,
  output O_P_S
);

  wire BIG_FRAC, xor_1_out;
  wire [31:0] A___B, A___B_t, ABS__A___B, negator_1_out;

  Multiplexer #(.enable("false")) multiplexer_1 (.in0(in_1), .in1(in_2), .out(O_P_S), .sel(in_5));
  Subtractor #(.width(32)) subtractor_1 (.a(in_3), .b(in_4), .out(A___B_t), .bout(BIG_FRAC));  // open: bin
  Multiplexer #(.width(32), .enable("false")) multiplexer_2 (
    .in0(A___B), .in1(ABS__A___B), .out(OUTPUT_SUM), .sel(xor_1_out));
  xor xor_1 (xor_1_out, in_1, in_2);
  Negator #(.width(32)) negator_1 (.in(A___B_t), .out(negator_1_out));
  Multiplexer #(.width(32), .enable("false")) multiplexer_3 (
    .in0(A___B_t), .in1(negator_1_out), .out(ABS__A___B), .sel(BIG_FRAC));
  Adder #(.width(32)) adder_1 (.a(in_3), .b(in_4), .out(A___B));  // open: cin, cout

  // Other names for the same wires on the sheet: BIG_EXP = in_5; F_FRAC_A[31:0] = in_3; F_FRAC_B[31:0] = in_4;
  //   SIGN_A = in_1; SIGN_B = in_2
endmodule

module rounder (
  input  [29:0] in_1,
  input  [8:0] in_2,
  input  in_3,
  output [21:0] O_P_FRACTION,
  output [8:0] O_P_EXP,
  output OVERFLOW
);

  wire adder_1_cout, adder_2_cout, all_1_1_out_2, or_1_out, ROUND;

  or or_1 (or_1_out, in_1[0], in_1[1], in_1[2], in_1[3], in_1[4], in_1[5], in_1[6], in_1[8]);
  and and_1 (ROUND, or_1_out, in_1[7]);
  Adder #(.width(22)) adder_1 (.a(in_1[29:8]), .b({22{1'b0}}), .out(O_P_FRACTION), .cin(ROUND), .cout(adder_1_cout));
  Adder #(.width(9)) adder_2 (.a(in_2), .b({9{1'b0}}), .out(O_P_EXP), .cin(adder_1_cout), .cout(adder_2_cout));
  all_1 all_1_1 (.in_1(in_2), .out_2(all_1_1_out_2));
  or or_2 (OVERFLOW, adder_2_cout, all_1_1_out_2, in_3);

  // Other names for the same wires on the sheet: NON_RONDED_SUM[29:0] = in_1; EXP[8:0] = in_2; OF = in_3
endmodule

module input_handler (
  input  [31:0] in_1,
  output [21:0] FRAC,
  output [8:0] EXP,
  output SIGN
);


  assign EXP = in_1[30:22];
  assign FRAC = in_1[21:0];
  assign SIGN = in_1[31];
endmodule

module output_handler (
  input  [21:0] FRAC,
  input  [8:0] EXP,
  input  SIGN,
  output [31:0] O_P,
  output NAN,
  output INF,
  output DeNorm
);

  wire EXP_ALL_0, EXP_ALL_1, FRAC_ATL_1, not_1_out;

  or or_1 (FRAC_ATL_1, FRAC[21], FRAC[20], FRAC[19], FRAC[18], FRAC[17], FRAC[16], FRAC[15], FRAC[14], FRAC[13], FRAC[12], FRAC[11], FRAC[9], FRAC[8], FRAC[7], FRAC[6], FRAC[5], FRAC[4], FRAC[3], FRAC[2], FRAC[1], FRAC[0], FRAC[10]);
  all_1 all_1_1 (.in_1(EXP), .out_2(EXP_ALL_1));
  nor nor_1 (EXP_ALL_0, EXP[8], EXP[7], EXP[6], EXP[5], EXP[4], EXP[3], EXP[2], EXP[1], EXP[0]);
  and and_1 (NAN, EXP_ALL_1, FRAC_ATL_1);
  not not_1 (not_1_out, FRAC_ATL_1);
  and and_2 (INF, not_1_out, EXP_ALL_1);
  and and_3 (DeNorm, FRAC_ATL_1, EXP_ALL_0);

  assign O_P = {SIGN, EXP, FRAC};
endmodule

module all_1 (
  input  [8:0] in_1,
  output out_2
);

  Comparator #(.width(9)) comparator_1 (.a(in_1), .b({9{1'b1}}), .eq(out_2));  // open: gt, lt
endmodule

module zero_flag (
  input  [31:0] in_1,
  input  [31:0] in_2,
  output ZERO_FLAG
);

  wire [31:31] not_1_out;

  not not_1 (not_1_out[31], in_1[31]);
  Comparator #(.width(32)) comparator_1 (.a({not_1_out[31], in_1[30:0]}), .b(in_2), .eq(ZERO_FLAG));  // open: gt, lt
endmodule
