// Logisim project 8_bit_pc.circ as structural Verilog: 4 circuits, main circuit main
module main (
  input  in_1,
  input  [7:0] in_2,
  output [19:0] out_3,
  output [7:0] out_4
);

  wire clock_1_out;
  wire [7:0] register_1_q;

  Register register_1 (.D(out_4), .Q(register_1_q), .clk(clock_1_out));  // open: en, clr
  Clock clock_1 (.out(clock_1_out));
  ROM #(.dataWidth(20)) rom_1 (.addr(register_1_q), .data(out_3));  // open: sel
  Adder adder_1 (.a(register_1_q), .b(in_2), .out(out_4));  // open: cin, cout

  // Notes on the sheet:
  //   contents of rom_1 (hex, n*v repeats v):
  //   ffff fffe
endmodule

module _8_bit_register (
  input  in_1,
  input  [7:0] write_bus,
  output [7:0] read_bus
);

  wire clock_1_out;
  wire [7:0] register_1_q;

  Register #(.trigger("falling")) register_1 (.D(write_bus), .Q(register_1_q), .clk(clock_1_out));  // open: en, clr
  Clock clock_1 (.out(clock_1_out));
  assign read_bus = in_1 ? register_1_q : 8'bz;  // Controlled_Buffer controlled_buffer_1

  // Other names for the same wires on the sheet: reg_write = in_1
endmodule

module _8_bit_zero_register (
  output [7:0] out_1
);


  assign out_1 = {8{1'b0}};
endmodule

module register_file (
  input  [7:0] in_1,
  input  [3:0] r_a,
  input  [3:0] r_b,
  input  [3:0] r_w
);

  wire sp, t_0, t_1, t_2, t_3, t_4, zero;

  Decoder #(.select(4), .enable("false")) decoder_1 (
    .out0(t_0), .out1(t_1), .out2(t_2), .out3(t_3), .out4(t_4), .out5(sp), .out6(zero), .sel(r_w));  // open: out7, out8, out9, out10, out11, out12, out13, out14, out15
  _8_bit_register u_8_bit_register_1 ();  // open: in_1, write_bus, read_bus
  _8_bit_register u_8_bit_register_2 ();  // open: in_1, write_bus, read_bus
  _8_bit_register u_8_bit_register_3 ();  // open: in_1, write_bus, read_bus
  _8_bit_register u_8_bit_register_4 ();  // open: in_1, write_bus, read_bus
  _8_bit_register u_8_bit_register_5 ();  // open: in_1, write_bus, read_bus
  _8_bit_register u_8_bit_register_6 ();  // open: in_1, write_bus, read_bus
  _8_bit_zero_register u_8_bit_zero_register_1 ();  // open: out_1

  // Other names for the same wires on the sheet: write_data[7:0] = in_1
endmodule
