// Logisim project single_cycle.circ as structural Verilog: 6 circuits, main circuit main
module main (
  input  in_1
);

  wire ALU_SRC, BEQ, BNEQ, CLK, JUMP, MEM_READ, MEM_TO_REG, MEM_WRITE, REG_DST, REG_WRITE, SHIFT, ZF;
  wire [1:0] bnj_selection_1_out_5;
  wire [2:0] ALU_OP;
  wire [3:0] multiplexer_2_out, OP_CODE, rd;
  wire [7:0] adder_1_out, adder_2_out, alu_input_1_input_1, alu_input_1_input_2, ALU_RES, immidiate,
       jump_add, multiplexer_1_out, multiplexer_4_out, R_DATA_2, ram_1_data, register_1_q,
       register_file_1_out_9, sp, t0, t1, t2, t3, t4, WRITE_DATA, zero;

  Clock clock_1 (.out(CLK));
  Adder adder_1 (.a(adder_2_out), .b(immidiate), .out(adder_1_out), .cin(1'b0));  // open: cout
  Multiplexer #(.select(2), .width(8), .enable("false")) multiplexer_1 (
    .in0(adder_2_out), .in1(adder_1_out), .in2(adder_1_out), .in3(jump_add), .out(multiplexer_1_out),
    .sel(bnj_selection_1_out_5));
  bnj_selection bnj_selection_1 (.in_1(BNEQ), .in_2(BEQ), .in_3(JUMP), .in_4(ZF), .out_5(bnj_selection_1_out_5));
  Register register_1 (.D(multiplexer_1_out), .Q(register_1_q), .clk(CLK), .clr(in_1));  // open: en
  Adder adder_2 (.a(8'h1), .b(register_1_q), .out(adder_2_out), .cin(1'b0));  // open: cout
  control_unit control_unit_1 (
    .OP_CODE(OP_CODE), .ALU_OP(ALU_OP), .ALU_SRC(ALU_SRC), .BNEQ(BNEQ), .BEQ(BEQ), .MEM_TO_REG(MEM_TO_REG),
    .MEM_WRITE(MEM_WRITE), .MEM_READ(MEM_READ), .REG_WRITE(REG_WRITE), .REG_DST(REG_DST), .SHIFT(SHIFT),
    .JUMP(JUMP));
  ROM #(.dataWidth(20)) rom_1 (.addr(register_1_q), .data({OP_CODE, jump_add, rd, immidiate[3:0]}));  // open: sel
  Multiplexer #(.width(4), .enable("false")) multiplexer_2 (
    .in0(jump_add[3:0]), .in1(rd), .out(multiplexer_2_out), .sel(REG_DST));
  Multiplexer #(.width(4), .enable("false")) multiplexer_3 (.in0(rd), .in1(4'b0000), .out(immidiate[7:4]), .sel(SHIFT));
  register_file register_file_1 (
    .R_A(jump_add[7:4]), .R_B(jump_add[3:0]), .R_W(multiplexer_2_out), .WD(WRITE_DATA), .in_5(REG_WRITE),
    .in_6(CLK), .in_7(in_1), .out_8(zero), .out_9(register_file_1_out_9), .out_10(t0), .out_11(R_DATA_2),
    .out_12(t1), .out_13(t2), .out_14(t3), .out_15(t4), .out_16(sp));
  Multiplexer #(.width(8), .enable("false")) multiplexer_4 (
    .in0(R_DATA_2), .in1(immidiate), .out(multiplexer_4_out), .sel(ALU_SRC));
  alu_input alu_input_1 (
    .in_1(register_file_1_out_9), .in_2(multiplexer_4_out), .in_3(SHIFT), .INPUT_1(alu_input_1_input_1),
    .INPUT_2(alu_input_1_input_2));
  // ALU_8_by_ART alu_8_by_art_1: pin names not known; wires that end beside it: alu_input_1_input_1, alu_input_1_input_2, ALU_OP, ZF, ALU_RES, ZF
  RAM #(.bus("separate")) ram_1 (
    .addr(ALU_RES), .din(R_DATA_2), .data(ram_1_data), .str(MEM_WRITE), .clk(CLK), .ld(MEM_READ), .clr(in_1));  // open: sel
  Multiplexer #(.width(8), .enable("false")) multiplexer_5 (
    .in0(ALU_RES), .in1(ram_1_data), .out(WRITE_DATA), .sel(MEM_TO_REG));

  // Other names for the same wires on the sheet: rt[3:0] = jump_add[3:0]; rs[3:0] = jump_add[7:4]; CLR = in_1;
  //   shft_amnt[3:0] = immidiate[3:0]

  // Notes on the sheet:
  //   contents of rom_1 (hex, n*v repeats v):
  //   b0010 90205
endmodule

module control_unit (
  input  [3:0] OP_CODE,
  output [2:0] ALU_OP,
  output ALU_SRC,
  output BNEQ,
  output BEQ,
  output MEM_TO_REG,
  output MEM_WRITE,
  output MEM_READ,
  output REG_WRITE,
  output REG_DST,
  output SHIFT,
  output JUMP
);

  ROM #(.addrWidth(4), .dataWidth(13)) rom_1 (
    .addr(OP_CODE),
    .data({ALU_OP, ALU_SRC, BNEQ, BEQ, MEM_TO_REG, MEM_WRITE, MEM_READ, REG_WRITE, REG_DST, SHIFT, JUMP}));  // open: sel

  // Notes on the sheet:
  //   contents of rom_1 (hex, n*v repeats v):
  //   608 e08 220 80c 480 1a0e c0c a08 1 208 100c c 40c 160e 258 500
endmodule

module register_file (
  input  [3:0] R_A,
  input  [3:0] R_B,
  input  [3:0] R_W,
  input  [7:0] WD,
  input  in_5,
  input  in_6,
  input  in_7,
  output [7:0] out_8,
  output [7:0] out_9,
  output [7:0] out_10,
  output [7:0] out_11,
  output [7:0] out_12,
  output [7:0] out_13,
  output [7:0] out_14,
  output [7:0] out_15,
  output [7:0] out_16
);

  wire and_1_out, and_2_out, and_3_out, and_4_out, and_5_out, and_6_out, SP_CLK, SP_EN, sp_en_t, t0_en,
       t1_en, t2_en, t3_en, t4_en, zero_en;
  wire [2:0] r_a_t, r_b_t, r_w_t;
  wire [7:0] SP_WRITE_DATA;

  Decoder #(.select(3), .enable("false")) decoder_1 (
    .out0(zero_en), .out1(t0_en), .out2(t1_en), .out3(t2_en), .out4(t3_en), .out5(t4_en), .out6(sp_en_t),
    .sel(r_w_t));  // open: out7
  _4_to_3 u_4_to_3_1 (.INPUT(R_A), .OUTPUT(r_a_t));
  _4_to_3 u_4_to_3_2 (.INPUT(R_B), .OUTPUT(r_b_t));
  _4_to_3 u_4_to_3_3 (.INPUT(R_W), .OUTPUT(r_w_t));
  and and_1 (and_1_out, sp_en_t, in_5);
  Multiplexer #(.width(8), .enable("false")) multiplexer_1 (.in0(WD), .in1(8'hfe), .out(SP_WRITE_DATA), .sel(in_7));
  Multiplexer #(.enable("false")) multiplexer_2 (.in0(and_1_out), .in1(in_7), .out(SP_EN), .sel(in_7));
  Multiplexer #(.enable("false")) multiplexer_3 (.in0(in_6), .in1(in_7), .out(SP_CLK), .sel(in_7));
  Register ZERO (.D(WD), .en(1'b0), .Q(out_8), .clk(in_6), .clr(in_7));
  Register T1 (.D(WD), .en(and_2_out), .Q(out_12), .clk(in_6), .clr(in_7));
  and and_2 (and_2_out, t1_en, in_5);
  Register T3 (.D(WD), .en(and_3_out), .Q(out_14), .clk(in_6), .clr(in_7));
  and and_3 (and_3_out, t3_en, in_5);
  Register SP (.D(SP_WRITE_DATA), .en(SP_EN), .Q(out_16), .clk(SP_CLK));  // open: clr
  and and_4 (and_4_out, t0_en, in_5);
  and and_5 (and_5_out, t2_en, in_5);
  and and_6 (and_6_out, t4_en, in_5);
  Register T0 (.D(WD), .en(and_4_out), .Q(out_10), .clk(in_6), .clr(in_7));
  Register T2 (.D(WD), .en(and_5_out), .Q(out_13), .clk(in_6), .clr(in_7));
  Register T4 (.D(WD), .en(and_6_out), .Q(out_15), .clk(in_6), .clr(in_7));
  Multiplexer #(.select(3), .width(8), .enable("false")) multiplexer_4 (
    .in0(out_8), .in1(out_10), .in2(out_12), .in3(out_13), .in4(out_14), .in5(out_15), .in6(out_16),
    .out(out_9), .sel(r_a_t));  // open: in7
  Multiplexer #(.select(3), .width(8), .enable("false")) multiplexer_5 (
    .in0(out_8), .in1(out_10), .in2(out_12), .in3(out_13), .in4(out_14), .in5(out_15), .in6(out_16),
    .out(out_11), .sel(r_b_t));  // open: in7

  // Other names for the same wires on the sheet: CLK = in_6; CLR = in_7; READ_DATA_1[7:0] = out_9;
  //   READ_DATA_2[7:0] = out_11; sp[7:0] = out_16; t0[7:0] = out_10; t1[7:0] = out_12; t2[7:0] = out_13;
  //   t3[7:0] = out_14; t4[7:0] = out_15; WRITE_DATA[7:0] = WD; WRITE_SIGNAL = in_5; zero[7:0] = out_8

  // Notes on the sheet:
  //   DEBUG
endmodule

module _4_to_3 (
  input  [3:0] INPUT,
  output [2:0] OUTPUT
);


  assign OUTPUT = INPUT[2:0];
endmodule

module alu_input (
  input  [7:0] in_1,
  input  [7:0] in_2,
  input  in_3,
  output [7:0] INPUT_1,
  output [7:0] INPUT_2
);

  Multiplexer #(.width(8), .enable("false")) multiplexer_1 (.in0(in_1), .in1(in_2), .out(INPUT_1), .sel(in_3));
  Multiplexer #(.width(8), .enable("false")) multiplexer_2 (.in0(in_2), .in1(in_1), .out(INPUT_2), .sel(in_3));

  // Other names for the same wires on the sheet: JUMP = in_3; READ_DATA_1[7:0] = in_1; READ_DATA_2[7:0] = in_2
endmodule

module bnj_selection (
  input  in_1,
  input  in_2,
  input  in_3,
  input  in_4,
  output [1:0] out_5
);

  wire and_1_out, and_2_out, not_1_out;

  and and_1 (and_1_out, in_1, not_1_out);
  not not_1 (not_1_out, in_4);
  and and_2 (and_2_out, in_4, in_2);
  or or_1 (out_5[0], and_1_out, in_3);
  or or_2 (out_5[1], in_3, and_2_out);

  // Other names for the same wires on the sheet: BEQ = in_2; BNEQ = in_1; JUMP = in_3; ZF = in_4
endmodule
